# Fritzing sketch Esquematico Ariyuu (saved by Fritzing 1.0.6)
breadboards: 1

parts:
  J1 = Basic Servo
  Lipo_1s = LIPO-2200mAh
  Mod1 = 2S-BMS
  Lipo_1s_2 = LIPO-2200mAh
  Lipo_1s_3 = LIPO-2200mAh
  Lipo_1s_4 = LIPO-2200mAh
  Mod2 = 2S-BMS
  Componente1 = Adafruit PCA9685 PWM/Servo Breakout [part_number=815]
  J2 = Basic Servo
  J3 = Basic Servo
  J4 = Basic Servo
  J5 = Basic Servo
  J6 = Basic Servo
  J7 = Basic Servo
  J8 = Basic Servo
  J9 = Basic Servo
  J10 = Basic Servo
  J11 = Basic Servo
  J12 = Basic Servo
  J13 = Basic Servo
  J14 = Basic Servo
  J15 = Basic Servo
  J16 = Basic Servo
  C1 = Electrolytic Capacitor [capacitance=4.3mF voltage=35V package="100 mil [THT, electrolytic]"]
  C2 = Ceramic Capacitor [capacitance=0.1mF voltage=35V package="100 mil [THT, multilayer]"]
  M1 = gy9250
  M2 = ESP32-S3-DevKitC-1-N8R8-v1 [part_number=ESP32-S3-DevKitC-1-N8R8-v1]
  J17 = Basic Servo
  Power_Bank1 = Generic USB Power Bank
  U1 = LM2596 step down module
  U2 = LM2596 step down module
  U3 = LM2596 step down module
  U4 = LM2596 step down module

nets:
  GND: J1.gnd, Mod2.pin3#2, Componente1.GND, J2.gnd, J3.gnd, J4.gnd, J5.gnd, J6.gnd, J7.gnd, J8.gnd, J10.gnd, J11.gnd, J12.gnd, J13.gnd, J14.gnd, J15.gnd, J16.gnd, C1.-, C2.0, M2.pin_23, M2.pin_24, M2.pin_44, Power_Bank1.Out_1_GND, U1.IN-, U1.OUT-, U2.IN-, U2.OUT-, U3.IN-, U3.OUT-, U4.IN-, U4.OUT-
  12v DC: J1.vcc, J2.vcc, J3.vcc, J4.vcc, J5.vcc, J6.vcc, J7.vcc, J8.vcc, J9.vcc, J10.vcc, J11.vcc, J12.vcc, J13.vcc, J14.vcc, J15.vcc, J16.vcc, C1.+, C2.1, J17.vcc, U1.OUT+, U2.OUT+, U3.OUT+, U4.OUT+
  Servo 1: J1.pulse
  N1: Lipo_1s.+, Mod1.pin1
  N2: Lipo_1s.-, Mod1.pin3#4, Lipo_1s_2.+
  N3: Mod1.pin2, Lipo_1s_2.-
  N4: Mod1.pin3#2, Mod2.pin3#3
  16.8 VDC: Mod1.pin3#3, U1.IN+, U2.IN+, U3.IN+, U4.IN+
  N5: Lipo_1s_3.+, Mod2.pin1
  N6: Lipo_1s_3.-, Lipo_1s_4.+, Mod2.pin3#4
  N7: Lipo_1s_4.-, Mod2.pin2
  S8: Componente1.PWM7
  S7: Componente1.PWM6
  S6: Componente1.PWM5
  S5: Componente1.PWM4
  S4: Componente1.PWM3
  S3: Componente1.PWM2
  S2: Componente1.PWM1
  S1: Componente1.PWM0
  3v DC: Componente1.VCC, M1.pin1, M2.pin_1
  SDA: Componente1.SDA, M1.pin4, M2.pin_15
  SCL: Componente1.SCL, M1.pin3, M2.pin_12
  S16: Componente1.PWM15
  S15: Componente1.PWM14
  S14: Componente1.PWM13
  S13: Componente1.PWM12
  S12: Componente1.PWM11
  S11: Componente1.PWM10
  S10: Componente1.PWM9
  S9: Componente1.PWM8
  Servo 2: J2.pulse
  Servo 4: J3.pulse
  Servo 3: J4.pulse
  Servo 6: J5.pulse
  Servo 7: J6.pulse
  Servo 8: J7.pulse
  Servo 5: J8.pulse
  GND P: J9.gnd, J17.gnd
  Servo 16: J9.pulse
  Servo 14: J10.pulse
  Servo 10: J11.pulse
  Servo 13: J12.pulse
  Servo 12: J13.pulse
  Servo 11: J14.pulse
  Servo 15: J15.pulse
  Servo 9: J16.pulse
  GND C: M1.pin2
  5v DC: M2.pin_21, Power_Bank1.Out_1_VCC
  Servo 17: M2.pin_40, J17.pulse

custom parts:
  LIPO-2200mAh: 2200mAh Lipo-battery
  2S-BMS: 2S-BMS LIPO battery charger / protection unit. Note pcb does not match the board as it will likely connect with wires, so pcb is 5 pads suitable for .1in header pins.
  Adafruit PCA9685 PWM/Servo Breakout: Using only two pins, control 16 free-running PWM outputs! I2C-controlled PWM driver with a built in clock. Unlike the TLC5940 family, you do not need to continuously send it signal tying up your microcontroller, its completely free running! 5V compliant, which means you can control it from a 3.3V microcontroller and still safely drive up to 6V outputs (this is good for when you want to control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
  gy9250: MPU-9250 module (three-axis gyroscope + three-axis acceleration + three-axis magnetic field). The generic model from ebay et. al. rather than the Sparkfun version.
  ESP32-S3-DevKitC-1-N8R8-v1: ESP32-S3-DevKitC-1-N8R8-v1 This module is 44pins long (2x22) and 11 pins width.
  Generic USB Power Bank: Many portable/mobile electronics builds (wearables, costumes, backpacks, standalone LED projects) are simply powered by an off-the-shelf USB power bank rather than a custom battery circuit. This generic part represents a multi-port USB power bank with a single, adjustable output voltage shared across all ports — matching how most commercial power banks behave — allowing the user to set the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
  LM2596 step down module: LM2596 DC-DC step down power supply module 3 A.
